# Fritzing sketch lcd_dht11 (saved by Fritzing 0.9.0b)
breadboards: 1

parts:
  Part1 = Arduino Uno (Rev3)
  part = Nokia5110LCDModule  # not connected
  DHT1 = DHT11 Humitidy and Temperature Sensor
  Nokia_5110_LCD_Module4 = Nokia5110 84x48
  Nokia_5110_LCD_Module5 = Nokia5110LCDModule

nets:
  N1: Part1.D2, DHT1.DATA
  N2: Part1.D3_PWM, Nokia_5110_LCD_Module4.RST, Nokia_5110_LCD_Module5.Vcc
  N3: Part1.D5_PWM, Nokia_5110_LCD_Module4.DC, Nokia_5110_LCD_Module5.SCE
  N4: Part1.D6_PWM, Nokia_5110_LCD_Module4.Din_(MOSI), Nokia_5110_LCD_Module5.RST
  N5: Part1.D7, Nokia_5110_LCD_Module4.SCLK, Nokia_5110_LCD_Module5.D/C
  3V3: Part1.3V3, Nokia_5110_LCD_Module4.Vcc, Nokia_5110_LCD_Module5.6_DN_(MOSI)
  5V: Part1.5V, DHT1.VDD, Nokia_5110_LCD_Module4.LED, Nokia_5110_LCD_Module5.SCLK
  GND: Part1.GND, DHT1.GND, Nokia_5110_LCD_Module4.Gnd, Nokia_5110_LCD_Module5.LED
  N6: Nokia_5110_LCD_Module4.CE, Nokia_5110_LCD_Module5.Grnd

custom parts:
  : Nokia 5110 LCD with 8 pin. It's a 45mm*45mm module part. Description: The Nokia 5110 is a basic graphic LCD screen for lots of applications. It was originally intended for as a cell phone screen. This one is mounted on an easy to solder PCB. It uses the PCD8544 controller. The PCD8544 is a low power CMOS LCD controller/driver, designed to drive a graphic display of 48 rows and 84 columns. All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
  DHT11 Humitidy and Temperature Sensor: DHT11 Humidity and Temperature Sensor
  : Nokia 5110 LCD with 8 pin. It's a 45mm*45mm module part. Description: The Nokia 5110 is a basic graphic LCD screen for lots of applications. It was originally intended for as a cell phone screen. This one is mounted on an easy to solder PCB. It uses the PCD8544 controller. The PCD8544 is a low power CMOS LCD controller/driver, designed to drive a graphic display of 48 rows and 84 columns. All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
