# Fritzing sketch esp32-turbidity-fritzing (saved by Fritzing 1.0.1rc)
breadboards: 1

parts:
  LED1 = LED - 3mm [color="Yellow (595nm)" current=0.030 package="3 mm [THT]"]
  LED2 = LED - 3mm [color="Red (633nm)" current=0.030 package="3 mm [THT]"]
  LED3 = LED - 3mm [color="Green (565nm)" current=0.030 package="3 mm [THT]"]
  LED4 = LED - 3mm [color="Green (560nm)" current=0.030 package="3 mm [THT]"]
  R1 = Resistor [tolerance=±5% power=0.25 resistance=220 package=THT]
  R2 = Resistor [tolerance=±5% power=0.25 resistance=220 package=THT]
  R3 = Resistor [tolerance=±5% power=0.25 resistance=220 package=THT]
  R4 = Resistor [tolerance=±5% power=0.25 resistance=220 package=THT]
  U3 = ESP32S-HiLetgo [part_number=ESP32S-HiLetgo]
  HC-SR04_Sensor_2 = HC-SR04 Ultrasonic Distance Sensor
  DHT2 = DHT11 Humitidy and Temperature Sensor
  Part3 = FC-28 Soil Hygrometer Module
  Part4 = FC-28 Soil Hygrometer Module - Probe
  U4 = Module 4 Relais 5V [package="Module 4 Relais 5V"]
  Grove2 = Grove OLED 128x96
  M2 = DC Motor [voltage_(max)=6V voltage_(min)=3V]

nets:
  GND: LED1.cathode, LED2.cathode, LED3.cathode, LED4.cathode, U3.GND, HC-SR04_Sensor_2.GND, DHT2.GND, Part3.GND, U4.GND, Grove2.GND, M2.pin_1
  N1: LED1.anode, R2.Pin_1
  N2: LED2.anode, R1.Pin_1
  N3: LED3.anode, R3.Pin_1
  N4: LED4.anode, R4.Pin_1
  N5: R1.Pin_0, U3.GPIO13
  N6: R2.Pin_0, U3.GPIO12
  N7: R3.Pin_0, U3.GPIO14
  N8: R4.Pin_0, U3.GPIO32
  N9: U3.GPIO34, Part3.AO
  N10: U3.GPIO33, U4.IN4
  N11: U3.GPIO25, U4.IN3
  N12: U3.GPIO26, U4.IN1
  N13: U3.GPIO27, U4.IN2
  VCC: U3.VIN, HC-SR04_Sensor_2.VCC, DHT2.VDD, Part3.VCC, U4.VCC, U4.K1-NF, Grove2.VCC
  N14: U3.GPIO4, DHT2.DATA
  N15: U3.GPIO5, HC-SR04_Sensor_2.TRIG
  N16: U3.GPIO18, HC-SR04_Sensor_2.ECHO
  N17: U3.GPIO21, Grove2.SDA
  N18: U3.GPIO22, Grove2.SCL
  N19: Part3.POS, Part4.POS
  N20: Part3.NEG, Part4.NEG
  N21: U4.K2-Com, U4.K1-NO, M2.pin_2

custom parts:
  ESP32S-HiLetgo: HiLetgo ESP-WROOM-32 ESP32 ESP-32S Development Board 2.4GHz Dual-Mode WiFi + Bluetooth Dual Cores Microcontroller The ESP32 integrated with Antenna switches, RF Balun, power amplifiers, low-noise amplifiers, filters, and management modules, and the entire solution occupies the least area of PCB. 2.4 GHz Wi-Fi plus Bluetooth dual-mode chip, with TSMC Ultra-low power consumption 40nm technology,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
  DHT11 Humitidy and Temperature Sensor: DHT11 Humidity and Temperature Sensor
  FC-28 Soil Hygrometer Module: The FC-28 is a soil hygrometer module that uses the Texas Instruments LM393 comparator chip to provide an analog measurement of soil humidity. The digital output is high when soil moisture is over a certain threshold, as determined by adjusting the potentiometer.
  FC-28 Soil Hygrometer Module - Probe: The FC-28 is a soil hygrometer module that uses the Texas Instruments LM393 comparator chip to provide an analog measurement of soil humidity.
  Module 4 Relais 5V: Module 4 Relais 5V 4x SPD-06VDC-SD-C
